# Fritzing sketch Lab_1_pot_pot (saved by Fritzing 0.9.3b)
breadboards: 1

parts:
  Part1 = Arduino Uno (Rev3)
  R1 = Rotary Potentiometer (Small) [maximum_resistance=100kΩ package=THT]
  R2 = Resistor [tolerance=±5% resistance=220 package=THT]
  LED2 = smd LED [color="Red (633nm)" package="0603 [SMD]"]
  LED3 = smd LED [color="Red (633nm)" package="0603 [SMD]"]
  LED4 = LED - 5mm [color="Red (633nm)" package="5 mm [THT]"]
  R4 = Resistor [tolerance=±5% resistance=220 package="2010 [SMD]"]
  R5 = Resistor [tolerance=±5% resistance=220 package="2010 [SMD]"]
  R6 = Rotary Potentiometer (Small) [maximum_resistance=100kΩ package=THT]

nets:
  N1: Part1.A0, R1.wiper
  N2: Part1.A1, R6.wiper
  N3: Part1.D9_PWM, LED3.anode
  N4: Part1.D10_PWM/SS, LED4.anode
  N5: Part1.D11_PWM/MOSI, LED2.anode
  N6: Part1.5V, R1.leg1, R6.leg2
  N7: Part1.GND, R1.leg2, R2.Pin_1, R4.Pin_1, R5.Pin_1, R6.leg1
  N8: R2.Pin_0, LED2.cathode
  N9: LED3.cathode, R4.Pin_0
  N10: LED4.cathode, R5.Pin_0
