# Fritzing sketch Schematic (saved by Fritzing 0.9.3b)
breadboards: 1

parts:
  Arduino_UNO_Rev3 = Arduino Uno (Rev3)
  Tilt_Servo = Basic Servo
  Pan_Servo = Basic Servo
  IR_Distance_Sensor = Infrared Proximity Sensor

nets:
  N1: Arduino_UNO_Rev3.A0, IR_Distance_Sensor.Vout
  N2: Arduino_UNO_Rev3.D3_PWM, Pan_Servo.pulse
  N3: Arduino_UNO_Rev3.D6_PWM, Tilt_Servo.pulse
  5V: Arduino_UNO_Rev3.5V, Tilt_Servo.vcc, Pan_Servo.vcc, IR_Distance_Sensor.Vcc
  GND: Arduino_UNO_Rev3.GND, Tilt_Servo.gnd, Pan_Servo.gnd, IR_Distance_Sensor.GND
